# Fritzing sketch weather-station (saved by Fritzing 0.9.4)
breadboards: 1

parts:
  Arduino_Uno = Arduino Uno (Rev3) - ICSP
  U1 = LCD-16X2 [package=lcd-16x2]
  U2 = POT [package=pot_mammoth]
  Part1 = Soil Moisture Sensor
  RHT1 = Humidity and Temperature Sensor RHT03
  R2 = PHOTOCELL [package=photocell-kit]
  R3 = Resistor [tolerance=±5% resistance=220 package=THT]
  IR1 = TSOP312.., 314.. [package=THT]
  Part4 = RFID-RC522-v3
  R4 = Resistor [tolerance=±5% resistance=220 package=THT]
  J1 = Piezo Speaker

nets:
  N1: Arduino_Uno.A0, Part1.SIG
  N2: Arduino_Uno.A1, R2.P$2, R3.Pin_0
  GND: Arduino_Uno.GND, U1.VSS, U1.R_W, U1.K, U2.E, Part1.GND, RHT1.GND_1, R3.Pin_1, IR1.GND, Part4.GND, J1.pin1
  N3: Arduino_Uno.D8, J1.pin2
  N4: Arduino_Uno.D9_PWM, Part4.RST
  N5: Arduino_Uno.D10_PWM/SS, Part4.SDA
  N6: Arduino_Uno.D11_PWM/MOSI, Part4.MOSI
  N7: Arduino_Uno.D12/MISO, Part4.MISO
  N8: Arduino_Uno.D13/SCK, Part4.SCK
  N9: Arduino_Uno.D0/RX, U1.E
  N10: Arduino_Uno.D1/TX, U1.RS
  N11: Arduino_Uno.D2, U1.DB7
  N12: Arduino_Uno.D3_PWM, U1.DB6
  N13: Arduino_Uno.D4, U1.DB5
  N14: Arduino_Uno.D5_PWM, U1.DB4
  N15: Arduino_Uno.D6_PWM, RHT1.Data-signal
  N16: Arduino_Uno.D7, IR1.Data
  3V3: Arduino_Uno.3V3, Part4.3.3V
  5V: Arduino_Uno.5V, U1.VDD, U2.A, RHT1.Vcc, R2.P$1, IR1.Vs, R4.Pin_0
  VIN: Arduino_Uno.VIN, Part1.VCC
  N17: U1.VO, U2.S
  N18: U1.A, R4.Pin_1

notes:
  RC522 bug, swappea GND por RST en esta vista

custom parts:
  RFID-RC522-v3: A simple China made RFID-RC522 Reader (6x4 cm); do check the pin labels, as this is a MFRC522 based clone.
